# Fritzing sketch iot_collaboration (saved by Fritzing 0.9.2b)
breadboards: 1

parts:
  Part1 = Arduino Nano (Rev3.0)
  T1 = TMP36 Temperature Sensor [package="TO92 [THT]"]

nets:
  GND: Part1.GND, T1.GND
  N1: Part1.5V, T1.+Vs
